# Fritzing sketch CoinSorter (saved by Fritzing 0.9.2b)
breadboards: 1

parts:
  Part1 = Arduino Micro (Rev3)  # not connected
  Part2 = Arduino Leonardo (Rev3b)
  IC1 = IC, DIP package, 16 pins [chip_label=TFT]
  D1 = SOLAR-IXYS [package=solarbit-12x1]
  J1 = Basic Servo
  J2 = Basic Servo
  LED1 = LED - 5mm [color="White (4500K)" package="5 mm [THT]"]
  R1 = Resistor [tolerance=±5% resistance=100 package=THT]
  R2 = Resistor [tolerance=±5% resistance=10k package=THT]
  S2 = Reed switch [package=THT]  # not connected

nets:
  N1: Part2.D2/SDA, IC1.pin7
  N2: Part2.D3_PWM/SCL, IC1.pin8
  N3: Part2.D4/A6, IC1.pin9
  N4: Part2.D5_PWM, IC1.pin10
  N5: Part2.D6_PWM/A7, IC1.pin11
  N6: Part2.D7, IC1.pin12
  N7: Part2.GND, IC1.pin6
  N8: Part2.A0, IC1.pin1
  N9: Part2.A1, IC1.pin2
  N10: Part2.A2, IC1.pin3
  N11: Part2.A3, IC1.pin4
  N12: Part2.A4, IC1.pin5
  N13: Part2.A5, D1.C
  N14: Part2.D8/A8, IC1.pin13
  N15: Part2.D9_PWM/A9, IC1.pin14
  N16: Part2.D10_PWM/A10, IC1.pin15
  N17: Part2.D11_PWM, R2.Pin_0
  GND: D1.A, J1.gnd, J2.gnd, LED1.cathode
  VCC: J1.vcc, J2.vcc
  N18: LED1.anode, R1.Pin_1
