# Fritzing sketch TFT (saved by Fritzing 0.9.2b)
breadboards: 1

parts:
  Part1 = Arduino Micro (Rev3)  # not connected
  Part2 = Arduino Leonardo (Rev3b)
  KEYPAD1 = Membrane Matrix Keypad  # not connected
  IC1 = IC, DIP package, 16 pins [chip_label=TFT]

nets:
  N1: Part2.D1/TX, IC1.pin11
  N2: Part2.D2/SDA, IC1.pin12
  N3: Part2.D3_PWM/SCL, Part2.D7, Part2.A3, IC1.pin5, IC1.pin10, IC1.pin14
  N4: Part2.D4/A6, IC1.pin8
  N5: Part2.D5_PWM, IC1.pin7
  N6: Part2.D6_PWM/A7, Part2.A4, IC1.pin6, IC1.pin9
  N7: Part2.GND, Part2.D10_PWM/A10, IC1.pin1
  N8: Part2.A0, Part2.D9_PWM/A9, IC1.pin2
  N9: Part2.A1, Part2.A2, Part2.D8/A8, IC1.pin3, IC1.pin4, IC1.pin15, IC1.pin16

custom parts:
  Membrane Matrix Keypad: Membrane Matrix 3x4 Keypad
